# Fritzing sketch schematic (saved by Fritzing 0.9.3b)

parts:
  BeagleBone = BeagleBone Black
  Current-limiting = Resistor [tolerance=±5% resistance=470 package=THT]
  Pull-down = Resistor [tolerance=±5% resistance=22k package=THT]
  Pull-down_2 = Resistor [tolerance=±5% resistance=22k package=THT]
  Keypad = mystery part, 14 pins [chip_label=Keypad]
  Pull-down1 = Resistor [tolerance=±5% resistance=22k package=THT]
  Pull-down2 = Resistor [tolerance=±5% resistance=22k package=THT]
  Pull-down3 = Resistor [tolerance=±5% resistance=22k package=THT]
  Pull-down4 = Resistor [tolerance=±5% resistance=22k package=THT]
  Pull-down5 = Resistor [tolerance=±5% resistance=22k package=THT]
  Pull-down6 = Resistor [tolerance=±5% resistance=22k package=THT]
  Pull-down7 = Resistor [tolerance=±5% resistance=22k package=THT]
  Pull-down8 = Resistor [tolerance=±5% resistance=22k package=THT]
  Pull-down9 = Resistor [tolerance=±5% resistance=22k package=THT]
  Pull-down10 = Resistor [tolerance=±5% resistance=22k package=THT]
  Current-limiting_2 = Resistor [tolerance=±5% resistance=470 package=THT]
  Call_LED = LED - 5mm [color="Red (633nm)" package="5 mm [THT]"]
  Current-limiting4 = Resistor [tolerance=±5% resistance=470 package=THT]
  Warning_LED = LED - 5mm [color="Red (633nm)" package="5 mm [THT]"]

nets:
  N1: BeagleBone.no_name_yet#3, Current-limiting.Pin_1
  N2: BeagleBone.no_name_yet#114, Call_LED.anode
  N3: BeagleBone.no_name_yet#116, Warning_LED.anode
  N4: BeagleBone.no_name_yet#132, Pull-down.Pin_0, Keypad.pin3
  N5: BeagleBone.no_name_yet#133, Pull-down_2.Pin_0, Keypad.pin4
  N6: BeagleBone.no_name_yet#134, Keypad.pin5, Pull-down1.Pin_0
  N7: BeagleBone.no_name_yet#135, Keypad.pin6, Pull-down2.Pin_0
  N8: BeagleBone.no_name_yet#136, Keypad.pin7, Pull-down3.Pin_0
  N9: BeagleBone.no_name_yet#137, Keypad.pin8, Pull-down4.Pin_0
  N10: BeagleBone.no_name_yet#138, Keypad.pin9, Pull-down5.Pin_0
  N11: BeagleBone.no_name_yet#139, Keypad.pin10, Pull-down6.Pin_0
  N12: BeagleBone.no_name_yet#140, Keypad.pin11, Pull-down7.Pin_0
  N13: BeagleBone.no_name_yet#142, Keypad.pin12, Pull-down10.Pin_0
  N14: BeagleBone.no_name_yet#145, Keypad.pin13, Pull-down8.Pin_0
  N15: BeagleBone.no_name_yet#146, Keypad.pin14, Pull-down9.Pin_0
  N16: BeagleBone.no_name_yet#201, Pull-down.Pin_1, Pull-down_2.Pin_1, Pull-down1.Pin_1, Pull-down2.Pin_1, Pull-down3.Pin_1, Pull-down4.Pin_1, Pull-down5.Pin_1, Pull-down6.Pin_1, Pull-down7.Pin_1, Pull-down8.Pin_1, Pull-down9.Pin_1, Pull-down10.Pin_1, Current-limiting_2.Pin_1, Current-limiting4.Pin_1
  N17: Current-limiting.Pin_0, Keypad.pin1
  N18: Current-limiting_2.Pin_0, Warning_LED.cathode
  N19: Call_LED.cathode, Current-limiting4.Pin_0

custom parts:
  BeagleBone Black: BeagleBone Black rev. A5B
